// Logisim project Monocycle-processor.circ as structural Verilog: 5 circuits, main circuit main
module main (
  input  in_1,
  output [23:0] out_2
);

  wire undriven;
  wire [4:0] multiplexer_1_out;
  wire [23:0] adder_1_out;
  wire [31:0] Address_Memory_out_2;

  PC pc_1 (.Address_Input(adder_1_out), .CLK(in_1), .Next_Address(out_2));
  Adder #(.width(24)) adder_1 (.a(out_2), .b(24'h1), .out(adder_1_out));  // open: cin, cout
  Address_Memory Address_Memory (.Instruction_Address(out_2), .out_2(Address_Memory_out_2));
  Multiplexer #(.width(5), .enable("false")) multiplexer_1 (
    .in0(Address_Memory_out_2[20:16]), .in1(Address_Memory_out_2[15:11]), .out(multiplexer_1_out),
    .sel(undriven));
  Data_Memory Data_Memory ();  // open: Memory_Address, Data, Mem_Read_Write, Readed_Data
  Multiplexer multiplexer_2 ();  // open: in0, in1, out, sel, en
endmodule

module PC (
  input  [23:0] Address_Input,
  input  CLK,
  output [23:0] Next_Address
);

  Counter #(.width(24), .max('hffffff)) counter_1 (
    .load(1'b1), .D(Address_Input), .count(1'b0), .Q(Next_Address), .clk(CLK));  // open: carry, clr
endmodule

// AM
module Address_Memory (
  input  [23:0] Instruction_Address,
  output [31:0] out_2
);

  ROM #(.addrWidth(24), .dataWidth(32)) rom_1 (.addr(Instruction_Address), .data(out_2));  // open: sel

  // Notes on the sheet:
  //   contents of rom_1 (hex, n*v repeats v):
  //   23bdffec afa80000 afa90004 afaa0008 afab000c afac0010 20082000 2009201c 8d2a0000 2001d8f1 102a0010
  //   21290004 200c0001 8d0a0000 8d2b0000 2001d8f1 102a000a 2001d8f1 102b0008 20010001 142c0001 ad0b0000
  //   21080004 21290004 2001ffff 71816002 800000d 8fa80000 8fa90004 8faa0008 8fab000c 8fac0010 23bd0014
  //   2402000a c
endmodule

// DM
module Data_Memory (
  input  [23:0] Memory_Address,
  input  [31:0] Data,
  input  Mem_Read_Write,
  output [31:0] Readed_Data
);

  wire not_1_out;

  not not_1 (not_1_out, Mem_Read_Write);
  RAM #(.addrWidth(24), .dataWidth(32), .bus("separate")) ram_1 (
    .addr(Memory_Address), .din(Data), .data(Readed_Data), .str(Mem_Read_Write), .ld(not_1_out));  // open: sel, clk, clr
endmodule

module Registers (
  input  [4:0] Read_Register_1,
  input  [4:0] Read_Register_2,
  input  [4:0] Write_Register,
  input  [31:0] Write_Data
);

  wire decoder_1_out0, decoder_1_out1, decoder_1_out2, decoder_1_out3, decoder_1_out4, decoder_1_out5,
       decoder_1_out6, decoder_1_out7, decoder_1_out8, decoder_1_out9, decoder_1_out10, decoder_1_out11,
       decoder_1_out12, decoder_1_out13, decoder_1_out14, decoder_1_out15, decoder_1_out16, decoder_1_out17,
       decoder_1_out18, decoder_1_out19, decoder_1_out20, decoder_1_out21, decoder_1_out22, decoder_1_out23,
       decoder_1_out24, decoder_1_out25, decoder_1_out26, decoder_1_out27, decoder_1_out28, decoder_1_out29,
       decoder_1_out30, decoder_1_out31, multiplexer_1_out, multiplexer_2_out;
  wire [31:0] register_1_q, register_2_q, register_3_q, register_4_q, register_5_q, register_6_q;

  Decoder #(.select(5), .enable("false")) decoder_1 (
    .out0(decoder_1_out0), .out1(decoder_1_out1), .out2(decoder_1_out2), .out3(decoder_1_out3),
    .out4(decoder_1_out4), .out5(decoder_1_out5), .out6(decoder_1_out6), .out7(decoder_1_out7),
    .out8(decoder_1_out8), .out9(decoder_1_out9), .out10(decoder_1_out10), .out11(decoder_1_out11),
    .out12(decoder_1_out12), .out13(decoder_1_out13), .out14(decoder_1_out14), .out15(decoder_1_out15),
    .out16(decoder_1_out16), .out17(decoder_1_out17), .out18(decoder_1_out18), .out19(decoder_1_out19),
    .out20(decoder_1_out20), .out21(decoder_1_out21), .out22(decoder_1_out22), .out23(decoder_1_out23),
    .out24(decoder_1_out24), .out25(decoder_1_out25), .out26(decoder_1_out26), .out27(decoder_1_out27),
    .out28(decoder_1_out28), .out29(decoder_1_out29), .out30(decoder_1_out30), .out31(decoder_1_out31),
    .sel(Write_Register));
  Register #(.width(32)) register_1 (.D(Write_Data), .en(decoder_1_out0), .Q(register_1_q));  // open: clk, clr
  Register #(.width(32)) register_2 (.D(Write_Data), .en(decoder_1_out1), .Q(register_2_q));  // open: clk, clr
  Register #(.width(32)) register_3 (.D(Write_Data), .en(decoder_1_out2), .Q(register_3_q));  // open: clk, clr
  Register #(.width(32)) register_4 (.D(Write_Data), .en(decoder_1_out3), .Q(register_4_q));  // open: clk, clr
  Register #(.width(32)) register_5 (.D(Write_Data), .en(decoder_1_out4), .Q(register_5_q));  // open: clk, clr
  Register #(.width(32)) register_6 (.D(Write_Data), .en(decoder_1_out5), .Q(register_6_q));  // open: clk, clr
  Register #(.width(32)) register_7 (.D(Write_Data), .en(decoder_1_out6));  // open: Q, clk, clr
  Register #(.width(32)) register_8 (.D(Write_Data), .en(decoder_1_out7));  // open: Q, clk, clr
  Register #(.width(32)) register_9 (.D(Write_Data), .en(decoder_1_out8));  // open: Q, clk, clr
  Register #(.width(32)) register_10 (.D(Write_Data), .en(decoder_1_out9));  // open: Q, clk, clr
  Register #(.width(32)) register_11 (.D(Write_Data), .en(decoder_1_out10));  // open: Q, clk, clr
  Register #(.width(32)) register_12 (.D(Write_Data), .en(decoder_1_out11));  // open: Q, clk, clr
  Register #(.width(32)) register_13 (.D(Write_Data), .en(decoder_1_out12));  // open: Q, clk, clr
  Register #(.width(32)) register_14 (.D(Write_Data), .en(decoder_1_out13));  // open: Q, clk, clr
  Register #(.width(32)) register_15 (.D(Write_Data), .en(decoder_1_out14));  // open: Q, clk, clr
  Register #(.width(32)) register_16 (.D(Write_Data), .en(decoder_1_out15));  // open: Q, clk, clr
  Register #(.width(32)) register_17 (.D(Write_Data), .en(decoder_1_out16));  // open: Q, clk, clr
  Register #(.width(32)) register_18 (.D(Write_Data), .en(decoder_1_out17));  // open: Q, clk, clr
  Register #(.width(32)) register_19 (.D(Write_Data), .en(decoder_1_out18));  // open: Q, clk, clr
  Register #(.width(32)) register_20 (.D(Write_Data), .en(decoder_1_out19));  // open: Q, clk, clr
  Register #(.width(32)) register_21 (.D(Write_Data), .en(decoder_1_out20));  // open: Q, clk, clr
  Register #(.width(32)) register_22 (.D(Write_Data), .en(decoder_1_out21));  // open: Q, clk, clr
  Register #(.width(32)) register_23 (.D(Write_Data), .en(decoder_1_out22));  // open: Q, clk, clr
  Register #(.width(32)) register_24 (.D(Write_Data), .en(decoder_1_out23));  // open: Q, clk, clr
  Register #(.width(32)) register_25 (.D(Write_Data), .en(decoder_1_out24));  // open: Q, clk, clr
  Register #(.width(32)) register_26 (.D(Write_Data), .en(decoder_1_out25));  // open: Q, clk, clr
  Register #(.width(32)) register_27 (.D(Write_Data), .en(decoder_1_out26));  // open: Q, clk, clr
  Register #(.width(32)) register_28 (.D(Write_Data), .en(decoder_1_out27));  // open: Q, clk, clr
  Register #(.width(32)) register_29 (.D(Write_Data), .en(decoder_1_out28));  // open: Q, clk, clr
  Register #(.width(32)) register_30 (.D(Write_Data), .en(decoder_1_out29));  // open: Q, clk, clr
  Register #(.width(32)) register_31 (.D(Write_Data), .en(decoder_1_out30));  // open: Q, clk, clr
  Register #(.width(32)) register_32 (.D(Write_Data), .en(decoder_1_out31));  // open: Q, clk, clr
  Multiplexer #(.select(5), .enable("false")) multiplexer_1 (
    .out(multiplexer_1_out), .sel(Read_Register_1));  // open: in0, in1, in2, in3, in4, in5, in6, in7, in8, in9, in10, in11, in12, in13, in14, in15, in16, in17, in18, in19, in20, in21, in22, in23, in24, in25, in26, in27, in28, in29, in30, in31
  Multiplexer #(.select(5), .enable("false")) multiplexer_2 (
    .out(multiplexer_2_out), .sel(Read_Register_2));  // open: in0, in1, in2, in3, in4, in5, in6, in7, in8, in9, in10, in11, in12, in13, in14, in15, in16, in17, in18, in19, in20, in21, in22, in23, in24, in25, in26, in27, in28, in29, in30, in31
endmodule
